# Fritzing sketch G7 - Portafrutta (saved by Fritzing 0.9.3b)
stripboards: 1

parts:
  J13 = screw terminal, 3 pins
  J8 = screw terminal, 3 pins
  Componente3 = HX711 Weighing Sensor Module
  Componente1 = HX711 Weighing Sensor Module
  Componente2 = HX711 Weighing Sensor Module
  Teensy_3_1 = Teensy 3.1  # not connected
  J9 = screw terminal, 6 pins

nets:
  GND: J13.pin1, J13.pin2, J13.pin3, Componente3.GND, Componente1.GND, Componente2.GND
  VCC: J8.pin1, J8.pin2, J8.pin3, Componente3.VCC, Componente1.VCC, Componente2.VCC
  N1: Componente3.DO/RX, J9.pin5
  N2: Componente3.CK/TX, J9.pin6
  N3: Componente1.DO/RX, J9.pin1
  N4: Componente1.CK/TX, J9.pin2
  N5: Componente2.DO/RX, J9.pin3
  N6: Componente2.CK/TX, J9.pin4

notes:
  USB 5V
  Load Cell
